// Digital circuit Praktikum 5 .dig as structural Verilog
module Praktikum_5 (
  input  A,
  input  B,
  input  C
);

  wire and_1_out, and_2_out, not_1_out, not_2_out, or_1_out, or_2_out;

  not not_1 (not_1_out, B);
  not not_2 (not_2_out, C);
  and and_1 (and_1_out, not_1_out, C);
  or or_1 (or_1_out, A, not_2_out);
  and and_2 (and_2_out, and_1_out, or_1_out);
  or or_2 (or_2_out, A, B, and_2_out);
  LED x (.in(or_2_out));

  // Notes on the sheet:
  //   A + !B * C (A+!C) +B
endmodule
