// Digital circuit Praktikum 6.dig as structural Verilog
module Praktikum_6 (
  input  A,
  input  B,
  output X
);

  wire not_1_out, not_2_out, or_1_out, or_2_out, or_3_out;

  not not_1 (not_1_out, B);
  not not_2 (not_2_out, A);
  or or_1 (or_1_out, A, B);
  or or_2 (or_2_out, A, not_1_out);
  or or_3 (or_3_out, not_2_out, B);
  and and_1 (X, or_1_out, or_2_out, or_3_out);

  // Notes on the sheet:
  //   (A+B)(A+!B)(!A+B)
endmodule
